// Logisim project Single_Cycle_CPU.circ as structural Verilog: 1 circuit, main circuit main
module main (
);

  wire and_1_out, Clk, clock_1_out, Halt, HasExp, IsCOP0, IsRet, multiplexer_1_out, multiplexer_3_out,
       multiplexer_4_out, not_2_out, or_1_out, undriven;

  Multiplexer multiplexer_1 (.out(multiplexer_1_out), .sel(and_1_out));  // open: in0, in1
  and and_1 (and_1_out, IsRet, IsCOP0);
  Multiplexer multiplexer_2 (.in0(clock_1_out), .in1(1'b0), .out(Clk), .sel(Halt));
  Clock clock_1 (.out(clock_1_out));
  Multiplexer multiplexer_3 (.in0(1'b0), .in1(multiplexer_1_out), .out(multiplexer_3_out), .sel(HasExp));
  not not_1 (HasExp, undriven);
  or or_1 (or_1_out, undriven, and_1_out);
  Register #(.width(1)) register_1 (.D(multiplexer_3_out), .clk(multiplexer_4_out));  // open: en, Q, clr
  Multiplexer multiplexer_4 (.in0(Clk), .in1(not_2_out), .out(multiplexer_4_out), .sel(or_1_out));
  not not_2 (not_2_out, Clk);
  // control_unit control_unit_1: pin names not known
  // CP0 cp0_1: pin names not known
endmodule
